# Fritzing sketch holobot (saved by Fritzing 0.9.1b)

parts:
  M2 = Stepper Motor - Unipolar
  Raspberry_Pi1 = Raspberry Pi B+  # not connected
  Part1 = EasyDriver_v44
  Part2 = EasyDriver_v44
  LPD8806_RGB_LED_Strip1 = LPD8806 RGB LED Strip
  M1 = Stepper Motor - Unipolar
  Part3 = Arduino Leonardo (Rev3b)
  Power_RGB1 = Prolight RGB 3 Watt Star
  Power_RGB2 = Prolight RGB 3 Watt Star
  Power_RGB3 = Prolight RGB 3 Watt Star
  Power_RGB4 = Prolight RGB 3 Watt Star
  Part4 = Arduino Motor Shield
  M3 = DC Motor
  R1 = Resistor [package="2512 [SMD]"]
  R2 = Resistor [package="2512 [SMD]"]
  R3 = Resistor [package="2512 [SMD]"]
  R4 = Resistor [package="2512 [SMD]"]
  IC1 = Voltage Regulator [package=to-92]
  J1 = Screw terminal - 2 pins [package=THT]
  J2 = Screw terminal - 2 pins [package=THT]
  J3 = Screw terminal - 2 pins [package=THT]
  J4 = Screw terminal - 2 pins [package=THT]
  VCC1 = Battery block 9V

nets:
  N1: M2.A, Part2.OUT2A
  N2: M2.COMMON_1, Part2.OUT2B
  N3: M2.COMMON_2, Part2.OUT1A
  N4: M2.D, Part2.OUT1B
  GND: Part1.GND, Part2.GND, Part3.GND
  N5: Part1.STEP, Part3.D4/A6
  N6: Part1.DIR, Part3.D2/SDA
  N7: Part1.OUT2A, M1.A
  N8: Part1.OUT2B, M1.COMMON_1
  N9: Part1.OUT1A, M1.COMMON_2
  N10: Part1.OUT1B, M1.D
  N11: Part1.ENABLE, Part3.D5_PWM
  N12: Part2.STEP, Part3.D7
  N13: Part2.DIR, Part3.D6_PWM/A7
  N14: Part2.ENABLE, Part3.D8/A8
  N15: LPD8806_RGB_LED_Strip1.GND, J4.pin2
  N16: LPD8806_RGB_LED_Strip1.DI, Part3.D9_PWM/A9
  N17: LPD8806_RGB_LED_Strip1.CI, Part3.D10_PWM/A10
  N18: LPD8806_RGB_LED_Strip1.+5V, J2.pin2
  N19: Power_RGB1.B+, R1.Pin_1
  N20: Power_RGB1.R-, Power_RGB2.B-, Power_RGB3.B-, Power_RGB4.B-, IC1.GND, J3.pin1, VCC1.-
  N21: Power_RGB2.B+, R3.Pin_1
  N22: Power_RGB3.B+, R2.Pin_1
  N23: Power_RGB4.B+, R4.Pin_1
  N24: Part4.OUT2, M3.pin_2
  N25: Part4.OUT1, M3.pin_1
  N26: R1.Pin_0, R2.Pin_0, R3.Pin_0, R4.Pin_0, IC1.IN, VCC1.+
  N27: IC1.OUT, J1.pin1

notes:
  Steppers

custom parts:
  LPD8806 RGB LED Strip: Digitally addressable RGB LED strip
